# Fritzing sketch Core (saved by Fritzing 0.9.3b)
circuit board: 7cm x 5cm
breadboards: 1

parts:
  J2 = female pin header, 14 pins [form="♀ (female)"]
  J1 = female pin header, 14 pins [form="♀ (female)"]
  J3 = female pin header, 4 pins [form="♀ (female)"]
  J4 = female pin header, 4 pins [form="♀ (female)"]
  J5 = female pin header, 4 pins [form="♀ (female)"]
  J9 = female pin header, 4 pins [form="♀ (female)"]
  J10 = female pin header, 4 pins [form="♀ (female)"]
  J11 = female pin header, 4 pins [form="♀ (female)"]
  LED1 = RGB LED - (4 legs) [package="5 mm [THT]"]
  X1 = USB Connectors [package=usb-b-pth]
  J12 = female pin header, 2 pins [form="♀ (female)"]
  J13 = female pin header, 2 pins [form="♀ (female)"]
  J16 = Power Jack [package=power_jack_slot]
  C10 = Electrolytic Capacitor [capacitance=10µF rated_voltage=35V package="100 mil [THT, electrolytic]"]
  C11 = Electrolytic Capacitor [capacitance=10µF rated_voltage=35V package="100 mil [THT, electrolytic]"]
  U4 = Voltage Regulator - 5V [package="TO220 [THT]"]
  R1 = Resistor [tolerance=±5% resistance=220 package=THT]
  R2 = Resistor [tolerance=±5% resistance=220 package=THT]
  R3 = Resistor [tolerance=±5% resistance=220 package=THT]
  R4 = Resistor [tolerance=±5% resistance=220 package=THT]
  R5 = Resistor [tolerance=±5% resistance=220 package=THT]
  J17 = female pin header, 1 pin [form="♀ (female)"]
  J18 = female pin header, 1 pin [form="♀ (female)"]
  J19 = female pin header, 1 pin [form="♀ (female)"]
  U5 = microSD Socket [package="Molex 502774-0891 [SMD]"]

nets:
  N1: J2.pin1, U5.DO
  N2: J2.pin2, U5.DI
  N3: J2.pin14, X1.GND
  N4: J1.pin1, U5.SCK
  N5: J1.pin2, U5.CS
  N6: J1.pin6, J9.pin2, J10.pin2, J11.pin2, R1.Pin_1
  N7: J1.pin7, J9.pin3, J10.pin3, J11.pin3, R2.Pin_1
  N8: J1.pin8, R3.Pin_1
  N9: J1.pin9, R4.Pin_1
  N10: J1.pin10, R5.Pin_1
  N11: J1.pin14, J9.pin4, J10.pin4, J11.pin4, J12.pin1, C11.+, U4.output_voltage, J17.pin1, J18.pin1
  N12: J3.pin1, J4.pin1, J5.pin1
  N13: J3.pin2, J4.pin2, J5.pin2
  N14: J3.pin3, J4.pin3, J5.pin3
  N15: J3.pin4, J4.pin4, J5.pin4
  GND: J9.pin1, J10.pin1, J11.pin1, LED1.common_anode, J16.GNDBREAK, J16.GND, C10.-, C11.-, U4.GND, J19.pin1
  N16: LED1.red_cathode, R5.Pin_0
  N17: LED1.green_cathode, R4.Pin_0
  N18: LED1.blue_cathode, R3.Pin_0
  N19: X1.D+, J13.pin1
  N20: X1.D-, J13.pin2
  N21: X1.VBUS, J12.pin2
  N22: J16.PWR, C10.+, U4.input_voltage
  N23: R1.Pin_0, R2.Pin_0
